// Digital circuit 4bitProcessor assignment 3.dig as structural Verilog
module _4bitProcessor_assignment_3 (
  input  clk,
  input  [3:0] Input,
  input  c_in,
  input  [3:0] in_4,
  input  Branch_Control_Signal,
  input  clk_2,
  input  clk_3,
  input  [1:0] ReadReg1_2,
  input  [1:0] ReadReg2_2,
  input  [1:0] WriteReg_2,
  input  [3:0] WriteData,
  input  WriteEnable,
  input  [3:0] ReadData1,
  input  [3:0] ReadData2_3,
  input  S0,
  input  S1,
  input  Cin,
  output out_6,
  output [3:0] Opcode,
  output [1:0] ReadReg1,
  output [1:0] ReadReg2,
  output [3:0] Branch_Address,
  output [1:0] WriteReg,
  output out_13,
  output [3:0] ReadData2,
  output [3:0] ReadData2_2,
  output [3:0] D,
  output out_28
);

  wire and_1_out, and_2_out, and_3_out, and_4_out, and_5_out, and_6_out, and_7_out, and_8_out,
       decoder_1_out_0, decoder_1_out_1, decoder_1_out_2, decoder_1_out_3, decoder_2_out_0, decoder_2_out_1,
       decoder_2_out_2, decoder_2_out_3, not_1_out, not_2_out, or_1_out, xor_1_out;
  wire [1:0] Counter_ovf;
  wire [3:0] Adder_s, Instruction_Memory_d, IR0_q, IR1_q, IR2_q, IR3_q, multiplexer_1_out, multiplexer_4_out,
       not_3_out, PC_q, R0_q, R2_q, R3_q;
  wire [15:15] ControlROM_d;

  xor xor_1 (xor_1_out, S0, Cin);
  Decoder #(.Selector_Bits(2)) decoder_1 (
    .sel(WriteReg_2), .out_0(decoder_1_out_0), .out_1(decoder_1_out_1), .out_2(decoder_1_out_2),
    .out_3(decoder_1_out_3));
  not not_1 (not_1_out, S0);
  not not_2 (not_2_out, S1);
  Add #(.Bits(4)) add_1 (.a(ReadData1), .b(multiplexer_1_out), .c_i(or_1_out), .s(D), .c_o(out_28));
  Register #(.Bits(4)) R0 (.D(WriteData), .C(clk_3), .en(and_1_out), .Q(R0_q));
  and and_1 (and_1_out, WriteEnable, decoder_1_out_0);
  assign not_3_out = ~ReadData2_3;  // Not not_3, 4 bits wide
  Multiplexer #(.Selector_Bits(2), .Bits(4)) multiplexer_1 (
    .sel({S1, S0}), .in_0(ReadData2_3), .in_1(not_3_out), .in_2(4'b0000), .in_3(4'b1111),
    .out(multiplexer_1_out));
  and and_2 (and_2_out, not_1_out, Cin);
  Multiplexer #(.Selector_Bits(2), .Bits(4)) multiplexer_2 (
    .sel(ReadReg1_2), .in_0(R0_q), .in_1(R0_q), .in_2(R2_q), .in_3(R3_q), .out(ReadData2));
  and and_3 (and_3_out, not_2_out, xor_1_out);
  Register #(.Bits(4)) R1 (.D(WriteData), .C(clk_3), .en(and_4_out), .Q(R0_q));
  and and_4 (and_4_out, WriteEnable, decoder_1_out_1);
  Multiplexer #(.Selector_Bits(2), .Bits(4)) multiplexer_3 (
    .sel(ReadReg2_2), .in_0(R0_q), .in_1(R0_q), .in_2(R2_q), .in_3(R3_q), .out(ReadData2_2));
  and and_5 (and_5_out, S1, and_2_out);
  Register #(.Bits(4)) R2 (.D(WriteData), .C(clk_3), .en(and_7_out), .Q(R2_q));
  Register #(.Bits(4)) R3 (.D(WriteData), .C(clk_3), .en(and_6_out), .Q(R3_q));
  and and_6 (and_6_out, WriteEnable, decoder_1_out_3);
  and and_7 (and_7_out, WriteEnable, decoder_1_out_2);
  or or_1 (or_1_out, and_5_out, and_3_out);
  Counter Counter (.en(1'b1), .C(clk_2), .clr(and_8_out), .out(Counter_ovf[0]), .ovf(Counter_ovf[1]));
  Register #(.Bits(4)) PC (.D(multiplexer_4_out), .C(clk), .en(Branch_Control_Signal), .Q(PC_q));
  and and_8 (and_8_out, Counter_ovf[0], Counter_ovf[1]);
  Add #(.Bits(4)) Adder (.a(PC_q), .b(in_4), .c_i(c_in), .s(Adder_s), .c_o(out_6));
  Multiplexer #(.Bits(4)) multiplexer_4 (
    .sel(Branch_Control_Signal), .in_0(Adder_s), .in_1(Input), .out(multiplexer_4_out));
  Register #(.Bits(4)) IR0 (.D(Instruction_Memory_d), .C(clk_2), .en(decoder_2_out_0), .Q(IR0_q));
  Register #(.Bits(4)) IR1 (.D(Instruction_Memory_d), .C(clk_2), .en(decoder_2_out_1), .Q(IR1_q));
  Register #(.Bits(4)) IR2 (.D(Instruction_Memory_d), .C(clk_2), .en(decoder_2_out_2), .Q(IR2_q));
  Register #(.Bits(4)) IR3 (.D(Instruction_Memory_d), .C(clk_2), .en(decoder_2_out_3), .Q(IR3_q));
  Decoder #(.Selector_Bits(2)) decoder_2 (
    .sel(Counter_ovf), .out_0(decoder_2_out_0), .out_1(decoder_2_out_1), .out_2(decoder_2_out_2),
    .out_3(decoder_2_out_3));
  // Probe on {IR3_q, IR2_q, IR1_q, IR0_q}
  ROM #(.AddrBits(4), .Bits(4)) Instruction_Memory (.A(PC_q), .sel(1'b1), .D(Instruction_Memory_d));
  ROM #(.AddrBits(16), .isProgramMemory("true"), .Bits(16)) ControlROM (
    .A({IR3_q, IR2_q, IR1_q, IR0_q}), .sel(1'b1),
    .D({ControlROM_d[15], Opcode, ReadReg1, ReadReg2, Branch_Address, WriteReg, out_13}));

  // Notes on the sheet:
  //   in_4: default 1
  //   S0'
  //   S1'
  //   effective_Cin
  //   contents of Instruction_Memory (hex, n*v repeats v):
  //   1,a
  //   contents of ControlROM (hex, n*v repeats v):
  //   101,2e,6b,1b
endmodule
