// Digital circuit ALU assignment 3.dig as structural Verilog
module ALU_assignment_3 (
  input  [3:0] ReadData1,
  input  [3:0] ReadData2,
  input  S0,
  input  S1,
  input  Cin,
  output [3:0] D,
  output out_7
);

  wire and_1_out, and_2_out, and_3_out, not_1_out, not_2_out, or_1_out, xor_1_out;
  wire [3:0] multiplexer_1_out, not_3_out;

  xor xor_1 (xor_1_out, S0, Cin);
  not not_1 (not_1_out, S0);
  not not_2 (not_2_out, S1);
  assign not_3_out = ~ReadData2;  // Not not_3, 4 bits wide
  Add #(.Bits(4)) add_1 (.a(ReadData1), .b(multiplexer_1_out), .c_i(or_1_out), .s(D), .c_o(out_7));
  and and_1 (and_1_out, not_1_out, Cin);
  Multiplexer #(.Bits(4), .Selector_Bits(2)) multiplexer_1 (
    .sel({S1, S0}), .in_0(ReadData2), .in_1(not_3_out), .in_2(4'b0000), .in_3(4'b1111),
    .out(multiplexer_1_out));
  and and_2 (and_2_out, not_2_out, xor_1_out);
  and and_3 (and_3_out, S1, and_1_out);
  or or_1 (or_1_out, and_3_out, and_2_out);

  // Notes on the sheet:
  //   S0'
  //   S1'
  //   effective_Cin
endmodule
