// Digital circuit Assignment2ALU.dig as structural Verilog
module Assignment2ALU (
  input  [3:0] A,
  input  [3:0] B,
  input  Cin,
  input  S0,
  input  S1,
  output [3:0] \output ,
  output out_6
);

  wire and_1_out, and_2_out, not_1_out, or_1_out, xor_1_out;
  wire [3:0] multiplexer_1_out, not_2_out;

  xor xor_1 (xor_1_out, Cin, S0);
  not not_1 (not_1_out, S1);
  and and_1 (and_1_out, not_1_out, xor_1_out);
  and and_2 (and_2_out, S1, or_1_out, not_1_out);
  Add #(.Bits(4)) add_1 (.a(A), .b(multiplexer_1_out), .c_i(or_1_out), .s(\output ), .c_o(out_6));
  or or_1 (or_1_out, and_1_out, and_2_out);
  assign not_2_out = ~B;  // Not not_2, 4 bits wide
  Multiplexer #(.Selector_Bits(2), .Bits(4)) multiplexer_1 (
    .sel({S1, S0}), .in_0(not_2_out), .in_1(B), .in_2(4'b0000), .in_3(4'b1111), .out(multiplexer_1_out));
endmodule
