// Digital circuit Assignment2RegisterFile.dig as structural Verilog
module Assignment2RegisterFile (
  input  clk,
  input  [3:0] Write_Data,
  input  [1:0] WriteReg,
  input  [1:0] ReadReg1,
  input  [1:0] ReadReg2,
  input  Ctrl_Reg
);

  wire and_1_out, and_2_out, and_3_out, and_4_out, decoder_1_out_0, decoder_1_out_1, decoder_1_out_2,
       decoder_1_out_3;
  wire [3:0] multiplexer_1_out, R0_q, R1_q, R2_q, R3_q;

  Register #(.Bits(4)) R0 (.D(Write_Data), .C(clk), .en(and_4_out), .Q(R0_q));
  Register #(.Bits(4)) R1 (.D(Write_Data), .C(clk), .en(and_3_out), .Q(R1_q));
  Register #(.Bits(4)) R2 (.D(Write_Data), .C(clk), .en(and_2_out), .Q(R2_q));
  Register #(.Bits(4)) R3 (.D(Write_Data), .C(clk), .en(and_1_out), .Q(R3_q));
  and and_1 (and_1_out, Ctrl_Reg, decoder_1_out_3);
  Multiplexer #(.Selector_Bits(2), .Bits(4)) multiplexer_1 (
    .sel(ReadReg1), .in_0(R0_q), .in_1(R1_q), .in_2(R2_q), .in_3(R3_q), .out(multiplexer_1_out));
  Multiplexer #(.Selector_Bits(2), .Bits(4)) multiplexer_2 (
    .sel(ReadReg2), .in_0(R0_q), .in_1(R1_q), .in_2(R2_q), .in_3(R3_q), .out(multiplexer_1_out));
  and and_2 (and_2_out, Ctrl_Reg, decoder_1_out_2);
  and and_3 (and_3_out, Ctrl_Reg, decoder_1_out_1);
  Decoder #(.Selector_Bits(2)) decoder_1 (
    .sel(WriteReg), .out_0(decoder_1_out_0), .out_1(decoder_1_out_1), .out_2(decoder_1_out_2),
    .out_3(decoder_1_out_3));
  and and_4 (and_4_out, Ctrl_Reg, decoder_1_out_0);
endmodule
