// Digital circuit Assignment2RegisterFile_ALU.dig as structural Verilog
module Assignment2RegisterFile_ALU (
  input  clk,
  input  [1:0] WriteReg,
  input  [1:0] ReadReg1,
  input  [1:0] ReadReg2,
  input  Ctrl_Reg,
  input  [3:0] A,
  input  [3:0] B,
  input  Cin,
  input  S2,
  input  S3,
  output [3:0] \output ,
  output out_11
);

  wire and_1_out, and_2_out, and_3_out, and_4_out, and_5_out, and_6_out, decoder_1_out_0, decoder_1_out_1,
       decoder_1_out_2, decoder_1_out_3, not_1_out, or_1_out, xor_1_out;
  wire [1:0] bussplitter_1_d;
  wire [3:0] not_2_out, R0_q, R1_q, R2_q, R3_q;

  xor xor_1 (xor_1_out, Cin, S2);
  not not_1 (not_1_out, S3);
  and and_1 (and_1_out, not_1_out, xor_1_out);
  and and_2 (and_2_out, S3, or_1_out, not_1_out);
  Add #(.Bits(4)) add_1 (.a(A), .b(A), .c_i(or_1_out), .s(\output ), .c_o(out_11));
  or or_1 (or_1_out, and_1_out, and_2_out);
  assign not_2_out = ~B;  // Not not_2, 4 bits wide
  Multiplexer #(.Bits(4)) multiplexer_1 (.sel(bussplitter_1_d[0]), .in_0(B), .in_1(not_2_out), .out(A));
  BusSplitter #(.Bits(2)) bussplitter_1 (.D(bussplitter_1_d), .D0(S2), .D1(S3));  // open: OE
  Register #(.Bits(4)) R0 (.D(\output ), .C(clk), .en(and_6_out), .Q(R0_q));
  Register #(.Bits(4)) R1 (.D(\output ), .C(clk), .en(and_5_out), .Q(R1_q));
  Register #(.Bits(4)) R2 (.D(\output ), .C(clk), .en(and_4_out), .Q(R2_q));
  Register #(.Bits(4)) R3 (.D(\output ), .C(clk), .en(and_3_out), .Q(R3_q));
  and and_3 (and_3_out, Ctrl_Reg, decoder_1_out_3);
  Multiplexer #(.Selector_Bits(2), .Bits(4)) multiplexer_2 (
    .sel(ReadReg1), .in_0(R0_q), .in_1(R1_q), .in_2(R2_q), .in_3(R3_q), .out(A));
  Multiplexer #(.Selector_Bits(2), .Bits(4)) multiplexer_3 (
    .sel(ReadReg2), .in_0(R0_q), .in_1(R1_q), .in_2(R2_q), .in_3(R3_q), .out(A));
  and and_4 (and_4_out, Ctrl_Reg, decoder_1_out_2);
  and and_5 (and_5_out, Ctrl_Reg, decoder_1_out_1);
  Decoder #(.Selector_Bits(2)) decoder_1 (
    .sel(WriteReg), .out_0(decoder_1_out_0), .out_1(decoder_1_out_1), .out_2(decoder_1_out_2),
    .out_3(decoder_1_out_3));
  and and_6 (and_6_out, Ctrl_Reg, decoder_1_out_0);
  // Pins of 1 and 2 bits meet at bussplitter_1_d
endmodule
