// Digital circuit Instruction Decoder assignment 3.dig as structural Verilog
module Instruction_Decoder_assignment_3 (
  input  [15:0] in_7,
  output [3:0] Opcode,
  output [1:0] ReadReg1,
  output [1:0] ReadReg2,
  output [3:0] Branch_Address,
  output [1:0] WriteReg,
  output out_6
);

  wire [15:15] ControlROM_d;

  ROM #(.AddrBits(16), .isProgramMemory("true"), .Bits(16)) ControlROM (
    .A(in_7), .sel(1'b1), .D({ControlROM_d[15], Opcode, ReadReg1, ReadReg2, Branch_Address, WriteReg, out_6}));

  // Notes on the sheet:
  //   contents of ControlROM (hex, n*v repeats v):
  //   101,2e,6b,1b
endmodule
