// Digital circuit Instruction Memory assignment 3.dig as structural Verilog
module Instruction_Memory_assignment_3 (
  input  [3:0] Address,
  output [3:0] Instruction
);

  ROM #(.AddrBits(4), .Bits(4)) Instruction_Memory (.A(Address), .sel(1'b1), .D(Instruction));
endmodule
