// Digital circuit Instruction Register IR.dig as structural Verilog
module Instruction_Register_IR (
  input  Data_from_DRAM,
  input  Alternative_Input,
  input  LD_Signal,
  input  clk,
  output Instructions_Out
);

  wire multiplexer_1_out;

  Multiplexer multiplexer_1 (.sel(LD_Signal), .in_0(Data_from_DRAM), .in_1(Alternative_Input), .out(multiplexer_1_out));
  Register Instruction_Register (.D(multiplexer_1_out), .C(clk), .en(LD_Signal), .Q(Instructions_Out));
endmodule
