// Digital circuit Instruction Register assignment 3.dig as structural Verilog
module Instruction_Register_assignment_3 (
  input  [3:0] Instr_Out,
  input  clk,
  output [15:0] IR_15_0
);

  wire and_1_out, decoder_1_out_0, decoder_1_out_1, decoder_1_out_2, decoder_1_out_3;
  wire [1:0] Counter_out;

  Counter Counter (.en(1'b1), .C(clk), .clr(and_1_out), .out(Counter_out[0]), .ovf(Counter_out[1]));
  and and_1 (and_1_out, Counter_out[0], Counter_out[1]);
  Register #(.Bits(4)) IR0 (.D(Instr_Out), .C(clk), .en(decoder_1_out_0), .Q(IR_15_0[3:0]));
  Register #(.Bits(4)) IR1 (.D(Instr_Out), .C(clk), .en(decoder_1_out_1), .Q(IR_15_0[7:4]));
  Register #(.Bits(4)) IR2 (.D(Instr_Out), .C(clk), .en(decoder_1_out_2), .Q(IR_15_0[11:8]));
  Register #(.Bits(4)) IR3 (.D(Instr_Out), .C(clk), .en(decoder_1_out_3), .Q(IR_15_0[15:12]));
  Decoder #(.Selector_Bits(2)) decoder_1 (
    .sel(Counter_out), .out_0(decoder_1_out_0), .out_1(decoder_1_out_1), .out_2(decoder_1_out_2),
    .out_3(decoder_1_out_3));
endmodule
