// Digital circuit Program Counter (PC).dig as structural Verilog
module Program_Counter__PC (
  input  INC,
  input  LD,
  input  RST,
  input  in_4,
  input  External_Address__A3__A2__A1__A0,
  output out_6
);

  wire add_1_s, multiplexer_1_out;

  Add add_1 (.a(INC), .b(LD), .c_i(1'b1), .s(add_1_s), .c_o(RST));
  Multiplexer multiplexer_1 (
    .sel(External_Address__A3__A2__A1__A0), .in_0(add_1_s), .in_1(LD), .out(multiplexer_1_out));
  Register Program_Counter (.D(multiplexer_1_out), .C(LD), .en(in_4), .Q(out_6));

  // Notes on the sheet:
  //   in_4: pin 0000
endmodule
