// Digital circuit Program Counter assignment 3.dig as structural Verilog
module Program_Counter_assignment_3 (
  input  clk,
  input  [3:0] Input,
  input  c_in,
  input  [3:0] in_4,
  input  Branch_Control_Signal,
  output out_6
);

  wire [3:0] Adder_s, multiplexer_1_out, PC_q;

  Register #(.Bits(4)) PC (.D(multiplexer_1_out), .C(clk), .en(Branch_Control_Signal), .Q(PC_q));
  Add #(.Bits(4)) Adder (.a(PC_q), .b(in_4), .c_i(c_in), .s(Adder_s), .c_o(out_6));
  Multiplexer #(.Bits(4)) multiplexer_1 (
    .sel(Branch_Control_Signal), .in_0(Adder_s), .in_1(Input), .out(multiplexer_1_out));

  // Notes on the sheet:
  //   in_4: default 1
endmodule
