// Digital circuit Register assignment 3.dig as structural Verilog
module Register_assignment_3 (
  input  clk,
  input  [1:0] ReadReg1,
  input  [1:0] ReadReg2,
  input  [1:0] WriteReg,
  input  [3:0] WriteData,
  input  WriteEnable,
  output [3:0] ReadData2,
  output [3:0] ReadData2_2
);

  wire and_1_out, and_2_out, and_3_out, and_4_out, decoder_1_out_0, decoder_1_out_1, decoder_1_out_2,
       decoder_1_out_3;
  wire [3:0] R0_q, R2_q, R3_q;

  Decoder #(.Selector_Bits(2)) decoder_1 (
    .sel(WriteReg), .out_0(decoder_1_out_0), .out_1(decoder_1_out_1), .out_2(decoder_1_out_2),
    .out_3(decoder_1_out_3));
  Register #(.Bits(4)) R0 (.D(WriteData), .C(clk), .en(and_1_out), .Q(R0_q));
  and and_1 (and_1_out, WriteEnable, decoder_1_out_0);
  Register #(.Bits(4)) R1 (.D(WriteData), .C(clk), .en(and_2_out), .Q(R0_q));
  and and_2 (and_2_out, WriteEnable, decoder_1_out_1);
  Multiplexer #(.Bits(4), .Selector_Bits(2)) multiplexer_1 (
    .sel(ReadReg1), .in_0(R0_q), .in_1(R0_q), .in_2(R2_q), .in_3(R3_q), .out(ReadData2));
  Register #(.Bits(4)) R2 (.D(WriteData), .C(clk), .en(and_4_out), .Q(R2_q));
  Multiplexer #(.Bits(4), .Selector_Bits(2)) multiplexer_2 (
    .sel(ReadReg2), .in_0(R0_q), .in_1(R0_q), .in_2(R2_q), .in_3(R3_q), .out(ReadData2_2));
  Register #(.Bits(4)) R3 (.D(WriteData), .C(clk), .en(and_3_out), .Q(R3_q));
  and and_3 (and_3_out, WriteEnable, decoder_1_out_3);
  and and_4 (and_4_out, WriteEnable, decoder_1_out_2);
endmodule
