// Digital circuit Registers_DRAM.dig as structural Verilog
module Registers_DRAM (
  input  LD,
  input  ST,
  input  CLR,
  input  [15:0] Address,
  input  [3:0] Data,
  input  Read_Write,
  input  Chip_Select,
  input  clk,
  output out_4,
  output [3:0] Data_Output
);

  wire register_1_q, register_2_q, register_3_q;

  Register register_1 (.D(LD), .C(ST), .en(CLR), .Q(register_1_q));
  RAMDualPort #(.AddrBits(16), .Bits(4)) ramdualport_1 (
    .A(Address), .Din(Data), .str(Read_Write), .C(clk), .ld(Chip_Select), .D(Data_Output));
  Register register_2 (.D(CLR), .C(ST), .en(LD), .Q(register_2_q));
  Multiplexer multiplexer_1 (.sel(register_1_q), .in_0(register_3_q), .in_1(register_2_q), .out(out_4));
  Register register_3 (.D(CLR), .C(ST), .en(LD), .Q(register_3_q));
  Register register_4 (.D(CLR), .C(ST), .en(LD), .Q(register_3_q));
endmodule
